# Fritzing sketch Schematic (saved by Fritzing 0.9.3b)
breadboards: 1

parts:
  U1 = NodeMCU V3.0
  LCD1 = LCD screen
  R1 = Trimmer Potentiometer [maximum_resistance=10kΩ package=THT]

nets:
  N1: U1.D2, LCD1.RS
  N2: U1.D3, LCD1.E
  3V3: U1.3V3, LCD1.VDD, LCD1.LED+
  N3: U1.GND#6, U1.GND#13, U1.GND#16, U1.GND#33, LCD1.VSS, LCD1.R/W, LCD1.LED-, R1.wiper
  N4: U1.D5, LCD1.DB4
  N5: U1.D6, LCD1.DB5
  N6: U1.D7, LCD1.DB6
  N7: U1.D8, LCD1.DB7
  N8: LCD1.V0, R1.leg2

custom parts:
  NodeMCU V3.0: ESP8266 based NodeMCU
